# Fritzing sketch Sketch_3_button (saved by Fritzing 0.9.3b)
breadboards: 1

parts:
  Part1 = Arduino Uno (Rev3)
  S1 = Pushbutton [package="[THT]"]
  R5 = Resistor [tolerance=±5% resistance=10k package=THT]

nets:
  N1: Part1.D2, S1.Pin_1, S1.Pin_2, R5.Pin_0
  N2: Part1.5V, S1.Pin_3, S1.Pin_4
  N3: Part1.GND, R5.Pin_1
