# Fritzing sketch Sketch_4_dice_game_decimal (saved by Fritzing 0.9.3b)
breadboards: 1

parts:
  Part1 = Arduino Uno (Rev3)
  R1 = Resistor [tolerance=±5% resistance=1k package=THT]
  R2 = Resistor [tolerance=±5% resistance=1k package=THT]
  LED2 = LED - 5mm [color="Red (633nm)" package="5 mm [THT]"]
  LED3 = LED - 5mm [color="Red (633nm)" package="5 mm [THT]"]
  R3 = Resistor [tolerance=±5% resistance=1k package=THT]
  LED4 = LED - 5mm [color="Red (633nm)" package="5 mm [THT]"]
  R4 = Resistor [tolerance=±5% resistance=1k package=THT]
  LED5 = LED - 5mm [color="Red (633nm)" package="5 mm [THT]"]
  S1 = Pushbutton [package="[THT]"]
  LED6 = LED - 5mm [color="Red (633nm)" package="5 mm [THT]"]
  R6 = Resistor [tolerance=±5% resistance=1k package=THT]
  R7 = Resistor [tolerance=±5% resistance=1k package=THT]
  LED7 = LED - 5mm [color="Red (633nm)" package="5 mm [THT]"]
  R8 = Resistor [tolerance=±5% resistance=10k package=THT]

nets:
  N1: Part1.D8, R6.Pin_1
  N2: Part1.D9_PWM, R4.Pin_1
  N3: Part1.D10_PWM/SS, R3.Pin_1
  N4: Part1.D11_PWM/MOSI, R2.Pin_1
  N5: Part1.D12/MISO, R1.Pin_1
  N6: Part1.GND, LED2.cathode, LED3.cathode, LED4.cathode, LED5.cathode, LED6.cathode, LED7.cathode, R8.Pin_1
  N7: Part1.D2, S1.Pin_1, S1.Pin_2, R8.Pin_0
  N8: Part1.D7, R7.Pin_1
  N9: Part1.5V, S1.Pin_3, S1.Pin_4
  N10: R1.Pin_0, LED2.anode
  N11: R2.Pin_0, LED3.anode
  N12: R3.Pin_0, LED4.anode
  N13: R4.Pin_0, LED5.anode
  N14: LED6.anode, R6.Pin_0
  N15: R7.Pin_0, LED7.anode
