# Fritzing sketch 9_joystick_controlled_robot_receiver (saved by Fritzing 0.9.3b)

parts:
  Part2 = Arduino Motor Shield (Rev3)
  M1 = DC Motor
  M3 = DC Motor
  VCC1 = 4 x AAA Battery Mount
  Part3 = Arduino Uno (Rev3)
  Part4 = NRF24L01+ Breakout Board

nets:
  N1: Part2.A0, Part3.A0
  N2: Part2.A1, Part3.A1
  N3: Part2.A2, Part3.A2
  N4: Part2.A3, Part3.A3
  N5: Part2.A4, Part2.SDA, Part3.A4/SDA, Part4.CE
  N6: Part2.A5, Part2.SCL, Part3.A5/SCL, Part4.CS
  N7: Part2.D8/BreakeB, Part3.D8
  N8: Part2.D9/BreakeA, Part3.D9_PWM
  N9: Part2.D10_PWM, Part3.D10_PWM/SS
  N10: Part2.D11_PWM/B, Part3.D11_PWM/MOSI
  N11: Part2.D12/DirA, Part3.D12/MISO
  N12: Part2.D13/DirB, Part3.D13/SCK
  GND: Part2.GND, VCC1.-, Part3.GND, Part4.GND
  N13: Part2.AREF, Part3.AREF
  N14: Part2.IOREF#118, Part3.D0/RX
  N15: Part2.D1/TX, Part3.D1/TX
  N16: Part2.D2, Part3.D2
  N17: Part2.D3_PWM/A, Part3.D3_PWM
  N18: Part2.D4, Part3.D4
  N19: Part2.D5_PWM, Part3.D5_PWM, Part4.MISO
  N20: Part2.D6_PWM, Part3.D6_PWM, Part4.MOSI
  N21: Part2.D7, Part3.D7, Part4.SCK
  N22: Part2.B-, M1.pin_2
  N23: Part2.B+, M1.pin_1
  N24: Part2.A-, M3.pin_2
  N25: Part2.A+, M3.pin_1
  N26: Part2.VMOT, VCC1.+
  N27: Part2.IOREF#147, Part3.ioref
  N28: Part2.RESET, Part3.RESET
  3V3: Part2.3V3, Part3.3V3, Part4.VCC
  5V: Part2.5V, Part3.5V
  VIN: Part2.VIN, Part3.VIN
