# Fritzing sketch Sketch_9_joystick_controlled_robot_transmitter (saved by Fritzing 0.9.3b)

parts:
  Part1 = Arduino Uno (Rev3)
  Part2 = NRF24L01+ Breakout Board
  Part3 = Thumb Joystick

nets:
  N1: Part1.A0, Part3.HORZ
  N2: Part1.A1, Part3.VERT
  N3: Part1.D8, Part2.CS
  N4: Part1.D11_PWM/MOSI, Part2.MOSI
  N5: Part1.D12/MISO, Part2.MISO
  N6: Part1.D13/SCK, Part2.SCK
  N7: Part1.D7, Part2.CE
  3V3: Part1.3V3, Part2.VCC
  5V: Part1.5V, Part3.VCC
  GND: Part1.GND, Part2.GND, Part3.GND
